# Fritzing sketch seven segment clock (saved by Fritzing 0.9.2b)
breadboards: 1

parts:
  Part1 = Arduino Nano (Rev3.0)
  S1 = Pushbutton [package="[THT]"]
  Power_plug1 = Power plug [part_number=12v]
  NEOPIXEL2 = Neopixel Strip -- White (30/m)
  RTC1 = DS1307 RTC Breakout

nets:
  GND: Part1.GND, S1.Pin_1, S1.Pin_2, Power_plug1.GND, NEOPIXEL2.GND, RTC1.GND
  N1: Part1.D2, NEOPIXEL2.Din
  N2: Part1.D3, S1.Pin_3, S1.Pin_4
  VIN: Part1.VIN, Power_plug1.VCC
  5V: Part1.5V, NEOPIXEL2.+5V, RTC1.5V
  N3: Part1.A5, RTC1.SCL
  N4: Part1.A4, RTC1.SDA

custom parts:
  Neopixel Strip -- White (30/m): These NeoPixel strips have 30 digitally-addressable pixel LEDs per meter and are very affordable and are only 12.5 mm wide, 10 mm if you remove the strip from the casing.
  DS1307 RTC Breakout: DS1307 Real-time Clock Breakout Board with Battery
